# Fritzing sketch TeensyWiring (saved by Fritzing 0.9.1b)
breadboards: 1

parts:
  U1 = LCD-16X2 [package=lcd-16x2]
  U2 = atmega328 [package=dip]
  Y2 = CRYSTAL [package=tc38h]
  22_picofarad = Capacitor [package=cap-pth-small2]
  22_picofarad_2 = Capacitor [package=cap-pth-small2]
  R1 = TRIMPOT [package=3362u-2]
  J1 = Infrared Proximity Sensor
  J2 = Piezo Speaker

nets:
  N1: U1.VSS, U1.R_W, U1.K, 22_picofarad.2, 22_picofarad_2.2, R1.CW
  N2: U1.VDD, R1.CCW
  N3: U1.VO, R1.WIPER
  N4: U1.RS, U2.D12
  N5: U1.E, U2.D11_(PWM)
  N6: U1.A, U2.D10_(PWM)
  N7: U2.D13, J1.Vout
  N8: Y2.1, 22_picofarad_2.1
  N9: Y2.2, 22_picofarad.1
  N10: J1.GND, J2.pin1
